# Fritzing sketch water_please (saved by Fritzing 0.9.0b)
circuit board: 5.43323cm x 3.63001cm
breadboards: 1

parts:
  Microduino1 = Microduino
  Q1 = NPN-Transistor [package="TO92 [THT]"]
  47 = Resistor [tolerance=±5% resistance=47 package=THT]
  Q2 = NPN-Transistor [package="TO92 [THT]"]
  47_2 = Resistor [tolerance=±5% resistance=47 package=THT]
  Sensor_2 = Header 1 [package=1x01_offset]
  Sensor2 = Header 1 [package=1x01_offset]
  JP4 = Header 1 [package=1x01_offset]
  Sensor_1 = Header 1 [package=1x01_offset]
  Pot2 = Trimmer Potentiometer [maximum_resistance=0.1MΩ package=THT]
  Pot1 = Trimmer Potentiometer [maximum_resistance=0.1MΩ package=THT]
  GRD = Header 1 [package=1x01_offset]
  VCC = Header 1 [package=1x01_offset]

nets:
  N1: Microduino1.GND, Q1.E, Q2.E, Pot2.leg1, Pot1.leg1, GRD.1
  N2: Microduino1.D7, Sensor2.1, JP4.1
  N3: Microduino1.3V3, VCC.1
  N4: Microduino1.A0, 47.Pin_0
  N5: Microduino1.A1, 47_2.Pin_0
  N6: Q1.B, Sensor_1.1, Pot1.wiper
  N7: Q1.C, 47.Pin_1
  N8: Q2.B, Sensor_2.1, Pot2.wiper
  N9: Q2.C, 47_2.Pin_1

custom parts:
  Microduino: The awesome Arduino compatible microcontroller
